// Logisim project ALU.circ as structural Verilog: 8 circuits, main circuit LeftShift32
module LeftShift32 (
  input  [31:0] B,
  input  Cin,
  input  [4:0] Sa,
  output [31:0] C
);

  wire [1:0] bit_extender_1_out;
  wire [3:0] bit_extender_2_out;
  wire [7:0] bit_extender_3_out;
  wire [15:0] bit_extender_4_out;
  wire [31:0] multiplexer_1_out, multiplexer_2_out, multiplexer_4_out;
  wire [31:8] multiplexer_3_out_2;
  wire [31:24] multiplexer_3_out;

  Multiplexer #(.width(32), .enable("false")) multiplexer_1 (
    .in0(B), .in1({B[30:0], Cin}), .out(multiplexer_1_out), .sel(Sa[0]));
  assign bit_extender_1_out = {{1{Cin}}, Cin};  // Bit_Extender bit_extender_1
  Multiplexer #(.width(32), .enable("false")) multiplexer_2 (
    .in0(multiplexer_1_out), .in1({multiplexer_1_out[29:0], bit_extender_1_out}), .out(multiplexer_2_out),
    .sel(Sa[1]));
  assign bit_extender_2_out = {{2{bit_extender_1_out[1]}}, bit_extender_1_out};  // Bit_Extender bit_extender_2
  Multiplexer #(.width(32), .enable("false")) multiplexer_3 (
    .in0(multiplexer_2_out), .in1({multiplexer_2_out[27:0], bit_extender_2_out}),
    .out({multiplexer_3_out, multiplexer_3_out_2}), .sel(Sa[2]));
  assign bit_extender_3_out = {{4{bit_extender_2_out[3]}}, bit_extender_2_out};  // Bit_Extender bit_extender_3
  Multiplexer #(.width(32), .enable("false")) multiplexer_4 (
    .in0({multiplexer_3_out, multiplexer_3_out_2}), .in1({multiplexer_3_out_2, bit_extender_3_out}),
    .out(multiplexer_4_out), .sel(Sa[3]));
  assign bit_extender_4_out = {{8{bit_extender_3_out[7]}}, bit_extender_3_out};  // Bit_Extender bit_extender_4
  Multiplexer #(.width(32), .enable("false")) multiplexer_5 (
    .in0(multiplexer_4_out), .in1({multiplexer_4_out[15:0], bit_extender_4_out}), .out(C), .sel(Sa[4]));
endmodule

module Add32 (
  input  [31:0] A,
  input  [31:0] B,
  input  Cin,
  output [31:0] C,
  output V
);

  wire adder1_1_cout, adder1_2_cout, adder2_1_cout, adder4_1_cout, adder8_1_cout, adder16_1_cout;

  Adder16 adder16_1 (.A(A[15:0]), .B(B[15:0]), .Cin(Cin), .Cout(adder16_1_cout), .S(C[15:0]));
  Adder8 adder8_1 (.A(A[23:16]), .B(B[23:16]), .Cin(adder16_1_cout), .Cout(adder8_1_cout), .S(C[23:16]));
  Adder4 adder4_1 (.A(A[27:24]), .B(B[27:24]), .Cin(adder8_1_cout), .Cout(adder4_1_cout), .S(C[27:24]));
  Adder2 adder2_1 (.Cin(adder4_1_cout), .A(A[29:28]), .B(B[29:28]), .Cout(adder2_1_cout), .S(C[29:28]));
  Adder1 adder1_1 (.A(A[30]), .B(B[30]), .Cin(adder2_1_cout), .S(C[30]), .Cout(adder1_1_cout));
  Adder1 adder1_2 (.A(A[31]), .B(B[31]), .Cin(adder1_1_cout), .S(C[31]), .Cout(adder1_2_cout));
  xor xor_1 (V, adder1_1_cout, adder1_2_cout);
endmodule

module ALU32 (
  input  [31:0] A,
  input  [31:0] B,
  input  [4:0] Sa,
  input  [3:0] Op,
  output [31:0] C,
  output V
);

  wire add32_1_v, and_1_out, and_3_out, nor_1_out, not_2_out, or_2_out, xnor_2_out, xor_2_out;
  wire [31:0] add32_1_c, and_2_out, bit_extender_1_out, bit_extender_2_out, leftshift32_1_c,
       multiplexer_1_out, multiplexer_2_out, multiplexer_3_out, multiplexer_4_out, multiplexer_5_out,
       multiplexer_6_out, multiplexer_7_out, multiplexer_8_out, nor_2_out, not_1_out, or_1_out, xnor_1_out,
       xor_1_out;

  and and_1 (and_1_out, B[31], Op[0], Op[2]);
  assign and_2_out = A & B;  // AND_Gate and_2, 32 bits wide
  assign or_1_out = B | A;  // OR_Gate or_1, 32 bits wide
  Multiplexer #(.width(32), .enable("false")) multiplexer_1 (
    .in0(B), .in1(not_1_out), .out(multiplexer_1_out), .sel(Op[2]));
  assign not_1_out = ~B;  // NOT_Gate not_1, 32 bits wide
  nor nor_1 (nor_1_out, A[0], A[1], A[2], A[3], A[4], A[5], A[6], A[7], A[8], A[9], A[10], A[11], A[12], A[13], A[14], A[15], A[17], A[18], A[19], A[20], A[21], A[22], A[23], A[24], A[25], A[26], A[27], A[28], A[29], A[30], A[31], A[16]);
  assign xor_1_out = A ^ B;  // XOR_Gate xor_1, 32 bits wide
  assign nor_2_out = ~(A | B);  // NOR_Gate nor_2, 32 bits wide
  assign xnor_1_out = ~(B ^ A);  // XNOR_Gate xnor_1, 32 bits wide
  Multiplexer #(.width(32), .enable("false")) multiplexer_2 (
    .in0(B),
    .in1({B[0], B[1], B[2], B[3], B[4], B[5], B[6], B[7], B[8], B[9], B[10], B[11], B[12], B[13], B[14], B[15], B[16], B[17], B[18], B[19], B[20], B[21], B[22], B[23], B[24], B[25], B[26], B[27], B[28], B[29], B[30], B[31]}),
    .out(multiplexer_2_out), .sel(Op[2]));
  and and_3 (and_3_out, xnor_1_out[15], xnor_1_out[0], xnor_1_out[1], xnor_1_out[2], xnor_1_out[3], xnor_1_out[4], xnor_1_out[5], xnor_1_out[6], xnor_1_out[7], xnor_1_out[8], xnor_1_out[9], xnor_1_out[10], xnor_1_out[11], xnor_1_out[12], xnor_1_out[13], xnor_1_out[14], xnor_1_out[16], xnor_1_out[17], xnor_1_out[18], xnor_1_out[19], xnor_1_out[20], xnor_1_out[21], xnor_1_out[22], xnor_1_out[23], xnor_1_out[24], xnor_1_out[25], xnor_1_out[26], xnor_1_out[27], xnor_1_out[28], xnor_1_out[29], xnor_1_out[30], xnor_1_out[31]);
  LeftShift32 leftshift32_1 (.B(multiplexer_2_out), .Cin(and_1_out), .Sa(Sa), .C(leftshift32_1_c));
  Add32 add32_1 (.A(A), .B(multiplexer_1_out), .Cin(Op[2]), .C(add32_1_c), .V(add32_1_v));
  or or_2 (or_2_out, nor_1_out, A[31]);
  xnor xnor_2 (xnor_2_out, or_2_out, Op[1]);
  assign bit_extender_1_out = {{31{1'b0}}, xnor_2_out};  // Bit_Extender bit_extender_1
  Multiplexer #(.width(32), .enable("false")) multiplexer_3 (
    .in0(xor_1_out), .in1(nor_2_out), .out(multiplexer_3_out), .sel(Op[1]));
  Multiplexer #(.width(32), .enable("false")) multiplexer_4 (
    .in0(and_2_out), .in1(or_1_out), .out(multiplexer_4_out), .sel(Op[1]));
  xor xor_2 (xor_2_out, and_3_out, Op[1]);
  assign bit_extender_2_out = {{31{1'b0}}, xor_2_out};  // Bit_Extender bit_extender_2
  Multiplexer #(.width(32), .enable("false")) multiplexer_5 (
    .in0({leftshift32_1_c[0], leftshift32_1_c[1], leftshift32_1_c[2], leftshift32_1_c[3], leftshift32_1_c[4], leftshift32_1_c[5], leftshift32_1_c[6], leftshift32_1_c[7], leftshift32_1_c[8], leftshift32_1_c[9], leftshift32_1_c[10], leftshift32_1_c[11], leftshift32_1_c[12], leftshift32_1_c[13], leftshift32_1_c[14], leftshift32_1_c[15], leftshift32_1_c[16], leftshift32_1_c[17], leftshift32_1_c[18], leftshift32_1_c[19], leftshift32_1_c[20], leftshift32_1_c[21], leftshift32_1_c[22], leftshift32_1_c[23], leftshift32_1_c[24], leftshift32_1_c[25], leftshift32_1_c[26], leftshift32_1_c[27], leftshift32_1_c[28], leftshift32_1_c[29], leftshift32_1_c[30], leftshift32_1_c[31]}),
    .in1(add32_1_c), .out(multiplexer_5_out), .sel(Op[1]));
  Multiplexer #(.width(32), .enable("false")) multiplexer_6 (
    .in0(multiplexer_4_out), .in1(bit_extender_2_out), .out(multiplexer_6_out), .sel(Op[0]));
  Multiplexer #(.width(32), .enable("false")) multiplexer_7 (
    .in0(leftshift32_1_c), .in1(add32_1_c), .out(multiplexer_7_out), .sel(Op[1]));
  Multiplexer #(.width(32), .enable("false")) multiplexer_8 (
    .in0(multiplexer_3_out), .in1(bit_extender_1_out), .out(multiplexer_8_out), .sel(Op[0]));
  Multiplexer #(.select(2), .width(32), .enable("false")) multiplexer_9 (
    .in0(multiplexer_7_out), .in1(multiplexer_5_out), .in2(multiplexer_6_out), .in3(multiplexer_8_out),
    .out(C), .sel(Op[3:2]));
  not not_2 (not_2_out, Op[3]);
  and and_4 (V, not_2_out, add32_1_v, Op[1]);

  // Notes on the sheet:
  //   10x0
  //   01xx
  //   10xx
  //   00xx
  //   11xx
endmodule

module Adder1 (
  input  A,
  input  B,
  input  Cin,
  output S,
  output Cout
);

  wire and_1_out, and_2_out, xor_1_out;

  xor xor_1 (xor_1_out, A, B);
  and and_1 (and_1_out, xor_1_out, Cin);
  and and_2 (and_2_out, A, B);
  xor xor_2 (S, xor_1_out, Cin);
  or or_1 (Cout, and_1_out, and_2_out);
endmodule

module Adder2 (
  input  Cin,
  input  [1:0] A,
  input  [1:0] B,
  output Cout,
  output [1:0] S
);

  wire adder1_1_cout;

  Adder1 adder1_1 (.A(B[0]), .B(A[0]), .Cin(Cin), .S(S[0]), .Cout(adder1_1_cout));
  Adder1 adder1_2 (.A(B[1]), .B(A[1]), .Cin(adder1_1_cout), .S(S[1]), .Cout(Cout));
endmodule

module Adder4 (
  input  [3:0] A,
  input  [3:0] B,
  input  Cin,
  output Cout,
  output [3:0] S
);

  wire adder2_1_cout;

  Adder2 adder2_1 (.Cin(Cin), .A(B[1:0]), .B(A[1:0]), .Cout(adder2_1_cout), .S(S[1:0]));
  Adder2 adder2_2 (.Cin(adder2_1_cout), .A(B[3:2]), .B(A[3:2]), .Cout(Cout), .S(S[3:2]));
endmodule

module Adder8 (
  input  [7:0] A,
  input  [7:0] B,
  input  Cin,
  output Cout,
  output [7:0] S
);

  wire adder4_1_cout;

  Adder4 adder4_1 (.A(A[3:0]), .B(B[3:0]), .Cin(Cin), .Cout(adder4_1_cout), .S(S[3:0]));
  Adder4 adder4_2 (.A(A[7:4]), .B(B[7:4]), .Cin(adder4_1_cout), .Cout(Cout), .S(S[7:4]));
endmodule

module Adder16 (
  input  [15:0] A,
  input  [15:0] B,
  input  Cin,
  output Cout,
  output [15:0] S
);

  wire adder8_1_cout;

  Adder8 adder8_1 (.A(A[7:0]), .B(B[7:0]), .Cin(Cin), .Cout(adder8_1_cout), .S(S[7:0]));
  Adder8 adder8_2 (.A(A[15:8]), .B(B[15:8]), .Cin(adder8_1_cout), .Cout(Cout), .S(S[15:8]));
endmodule
